# Fritzing sketch led-strip (saved by Fritzing 0.9.3b)

parts:
  Part1 = Arduino Uno (Rev3)
  NEOPIXEL1 = Neopixel Strip -- White (60/m) [part_number=1138]

nets:
  N1: Part1.D6_PWM, NEOPIXEL1.DI
  5V: Part1.5V, NEOPIXEL1.+5V
  GND: Part1.GND, NEOPIXEL1.GND

custom parts:
  Neopixel Strip -- White (60/m): Neopixel Strip, White, 60 pixels per meter.
